# Fritzing sketch tervezet (saved by Fritzing 0.9.10b)
breadboards: 1

parts:
  Part1 = Arduino Nano (Rev3.0)
  U1 = POT [knob_status=50% power=0.5W package=pot_mammoth]  # not connected
  S1 = Pushbutton [package="[SMD]"]
  Disp1 = 38mm 8x8 dot matrix row cathode led display with standard pcb pads  # not connected
  SG1 = Buzzer 12mm [package=buzzer-12mm-ns]  # not connected
  SEN1 = US-100 Ultrasonic Distance Sensor  # not connected
  D1 = LED_BARGRAPH_10 [package=led_bargaph_10]  # not connected
  Driver1 = 28BYJ-48 Driver Module [part_number=ULN2003 package=THT]
  SM1 = 28BYJ-48 Stepper Motor [part_number=28BYJ-48]
  VCC1 = Battery

nets:
  N1: Part1.D9, Driver1.IN4
  N2: Part1.D10, Driver1.IN3
  N3: Part1.D11/MOSI, Driver1.IN2
  N4: Part1.D12/MISO, Driver1.IN1
  N5: S1.Pin_1, S1.Pin_2
  N6: S1.Pin_3, S1.Pin_4
  N7: Driver1.GND, VCC1.-
  N8: Driver1.Vmotor, VCC1.+
  N9: Driver1.blue-pin, SM1.blue-pin
  N10: Driver1.pink-pin, SM1.pink-pin
  N11: Driver1.yellow-pin, SM1.yellow-pin
  N12: Driver1.orange-pin, SM1.orange-pin
  N13: Driver1.red-pin, SM1.red-pin

custom parts:
  28BYJ-48 Driver Module: ULN2003 Driver Module for the 28BYJ-48 Unipolar Stepper Motor LED A - Blue wire - Bottom coil left LED B - Pink wire - Top coil left LED C - Yellow wire - Bottom coil right LED D - Orange wire - Top coil right Common rail - red Connector pins: blue - pink - yellow - orange - red Control pins - IN1 to IN4 Power pins - GND & Vmotor (5-12V) On/Off jumper (if removed, power to motor is cut).
  28BYJ-48 Stepper Motor: Unipolar Stepper Motor 28BYJ-48 Top coil - pink & orange Bottom coil - blue & yellow Common rail - red Connector pins: blue - pink - yellow - orange - red
